// Digital circuit memory_Module.dig as structural Verilog
module memory_Module (
  input  [3:0] Clear,
  input  Clock,
  input  [3:0] Data,
  input  [1:0] SP,
  input  [3:0] A
);

  Demultiplexer #(.Selector_Bits(4), .Bits(2)) demultiplexer_1 (
    .sel(A), .in(SP));  // open: out_0, out_1, out_2, out_3, out_4, out_5, out_6, out_7, out_8, out_9, out_10, out_11, out_12, out_13, out_14, out_15
  // _4_bit_register Register_0: pin names not known; wires that end beside it: Clock, Clear
  // _4_bit_register Register_1: pin names not known; wires that end beside it: Clock, Clear
  // _4_bit_register Register_2: pin names not known; wires that end beside it: Clock, Clear
  // _4_bit_register Register_3: pin names not known; wires that end beside it: Clock, Clear
  // _4_bit_register Register_4: pin names not known; wires that end beside it: Clock, Clear
  // _4_bit_register Register_5: pin names not known; wires that end beside it: Clock
  // _4_bit_register Register_6: pin names not known; wires that end beside it: Clock
  // _4_bit_register Register_7: pin names not known; wires that end beside it: Clear, Clock
  // _4_bit_register Register_8: pin names not known; wires that end beside it: Clock
  // _4_bit_register Register_9: pin names not known; wires that end beside it: Clock
  // _4_bit_register Register_10: pin names not known; wires that end beside it: Clock
  // _4_bit_register Register_11: pin names not known; wires that end beside it: Clock
  // _4_bit_register Register_12: pin names not known; wires that end beside it: Clock
  // _4_bit_register Register_13: pin names not known; wires that end beside it: Clock
  // _4_bit_register Register_14: pin names not known; wires that end beside it: Clock
  // _4_bit_register Register_15: pin names not known; wires that end beside it: Clock
  // Pins of 1 and 4 bits meet at A
endmodule
